# Fritzing sketch Sketsa Blynk (saved by Fritzing 0.9.3b)
breadboards: 1

parts:
  U1 = ESP32-38PinWide [part_number=ESP32-38PinWide]
  R1 = Photocell (LDR) [package=THT]
  DHT1 = DHT11 Humitidy and Temperature Sensor (3 pins)
  LED1 = smd LED [color="Red (633nm)" package="0603 [SMD]"]
  LED2 = smd LED [color="Red (633nm)" package="0603 [SMD]"]

nets:
  N1: U1.3.3, DHT1.VDD
  GND: U1.GND, U1.GPIO2, R1.pin_1, DHT1.GND, LED1.cathode, LED2.cathode
  N2: U1.GPIO15, LED1.anode
  N3: U1.GPIO17, LED2.anode
  N4: U1.GPIO1, DHT1.DATA

custom parts:
  ESP32-38PinWide: Generic 38-Pin ESP32 with wide format (only access to one side of pins on a breadboard) based on Stephen Lilley's HiLetgo ESP-WROOM-32 ESP32 ESP-32S Development Board.
  DHT11 Humitidy and Temperature Sensor (3 pins): DHT11 Humidity and Temperature Sensor (3 pins) from the design created by John De Cristofaro for Adafruit Industries.
